// Logisim project Daniels project.circ as structural Verilog: 1 circuit, main circuit main
module main (
  input  in_1,
  input  in_2,
  input  in_3,
  input  in_4,
  output out_5,
  output out_6,
  output out_7,
  output out_8,
  output out_9,
  output out_10
);

  wire j_k_ff_1_qn, j_k_ff_2_qn, j_k_ff_3_qn, j_k_ff_4_qn, j_k_ff_5_qn, nand_2_out, not_1_out, not_2_out,
       not_3_out, not_4_out;

  not not_1 (not_1_out, j_k_ff_1_qn);
  not not_2 (not_2_out, j_k_ff_2_qn);
  J_K_Flip_Flop j_k_ff_1 (
    .J(j_k_ff_1_qn), .clk(in_2), .K(not_1_out), .Q(out_6), .Qn(j_k_ff_1_qn));  // open: preset, en, reset
  nand nand_1 (out_9, in_3, in_3);
  nand nand_2 (nand_2_out, j_k_ff_3_qn, j_k_ff_3_qn);
  J_K_Flip_Flop j_k_ff_2 (
    .J(j_k_ff_2_qn), .clk(in_1), .K(not_2_out), .Q(out_5), .Qn(j_k_ff_2_qn));  // open: preset, en, reset
  not not_3 (not_3_out, j_k_ff_4_qn);
  J_K_Flip_Flop j_k_ff_3 (
    .J(j_k_ff_3_qn), .clk(in_4), .K(nand_2_out), .Q(out_10), .Qn(j_k_ff_3_qn));  // open: preset, en, reset
  J_K_Flip_Flop j_k_ff_4 (
    .J(j_k_ff_4_qn), .clk(j_k_ff_1_qn), .K(not_3_out), .Q(out_7), .Qn(j_k_ff_4_qn));  // open: preset, en, reset
  not not_4 (not_4_out, j_k_ff_5_qn);
  J_K_Flip_Flop j_k_ff_5 (
    .J(j_k_ff_5_qn), .clk(j_k_ff_4_qn), .K(not_4_out), .Q(out_8), .Qn(j_k_ff_5_qn));  // open: preset, en, reset

  // Notes on the sheet:
  //   Making NOT gates out of NAND GATES
  //   This is an amplified version of the three circuits below for better reading
  //   Make one of these first and then you can move onto connecting them together like below
endmodule
